# Fritzing sketch Bathroom (saved by Fritzing 0.9.3b)
breadboards: 1

parts:
  U1 = NodeMCU V1.0
  DHT1 = DHT11 Humitidy and Temperature Sensor (3 pins)
  D1 = LTE-302 [package=lte-302]
  R1 = Resistor [tolerance=±5% resistance=220 package=THT]

nets:
  N1: U1.D3, R1.Pin_0
  N2: U1.D4, DHT1.VDD, D1.A
  N3: U1.3V3, DHT1.DATA
  GND: U1.GND, DHT1.GND
  N4: D1.C, R1.Pin_1

custom parts:
  NodeMCU V1.0: ESP8266 based NodeMCU
  DHT11 Humitidy and Temperature Sensor (3 pins): DHT11 Humidity and Temperature Sensor (3 pins) from the design created by John De Cristofaro for Adafruit Industries.
